# Fritzing sketch cansat (saved by Fritzing 0.9.3b)

parts:
  MCU1 = Raspberry Pi Zero  # not connected
  Part1 = Adafruit BME680 [part_number="Adafruit #3660"]
  Part2 = Adafruit Feather RP2040 [part_number="Adafruit #4884"]
  U1 = LIPO-2000mAh [package=lipo-2000]

nets:
  N1: Part1.SDI/SDA, Part2.SDA
  GND: Part1.GND, Part2.GND, U1.-
  VCC: Part1.VCC, Part2.+3V3
  N2: Part1.SCK/SCL, Part2.SCL
  N3: Part2.VBAT, U1.+

custom parts:
  Adafruit Feather RP2040: A new chip means a new Feather, and the Raspberry Pi RP2040 is no exception. When we saw this chip we thought "this chip is going to be awesome when we give it the Feather Treatment" and so we did! This Feather features the RP2040, and all niceties you know and love about Feather Measures 2.0" x 0.9" x 0.28" (50.8mm x 22.8mm x 7mm) without headers soldered in Light as a (large?) feather - 5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
